// Logisim project branch-comp.circ as structural Verilog: 1 circuit, main circuit branch_comp
module branch_comp (
  input  [31:0] rs1,
  input  [31:0] rs2,
  input  BrUn,
  output BrEq,
  output BrLt
);

  Comparator #(.width(32)) comparator_1 (.a(rs1), .b(rs2));  // open: gt, eq, lt
  Comparator #(.width(32)) comparator_2 (.a(rs1), .b(rs2));  // open: gt, eq, lt

  // Notes on the sheet:
  //   INPUTS to your circuit
  //   DON'T CHANGE THE LOCATIONS OF THE INPUTS AND OUTPUTS!
  //   OUTPUT from your circuit
endmodule
