// Logisim project cpu.circ as structural Verilog: 1 circuit, main circuit cpu
module cpu (
  input  clk,
  input  [31:0] INSTRUCTION,
  input  [31:0] MEM_READ_DATA,
  output [31:0] MEM_WRITE_ADDRESS,
  output [31:0] PROGRAM_COUNTER,
  output [31:0] ra,
  output [31:0] sp,
  output [31:0] t0,
  output [31:0] t1,
  output [31:0] t2,
  output [31:0] s0,
  output [31:0] s1,
  output [31:0] a0,
  output [31:0] tohost,
  output [3:0] MEM_WRITE_ENABLE,
  output [31:0] MEM_WRITE_DATA
);

  wire ASel, BrEq, BrLt, BrUn, BSel, CSR_address, CSRSel, CSRWen, MemRW, PCSel, RegWEn;
  wire [1:0] WBSel;
  wire [2:0] control_logic_1_immsel;
  wire [3:0] ALUSel;
  wire [4:0] bit_extender_3_out, bit_extender_4_out, shifter_4_out, shifter_6_out;
  wire [7:0] load_lb;
  wire [15:0] load_lh;
  wire [31:0] ALUResult, CSR_din, imm, load_lb_ext, load_lh_ext, load_lw, multiplexer_1_out,
       multiplexer_2_out, multiplexer_3_out, PC4, pc4_t, rd_output_load, Read_Data_1, Read_Data_2, sb_store,
       sh_store, shifter_1_out, shifter_2_out, shifter_3_out, shifter_5_out, WBSelOutput, WriteData;

  Adder #(.width(32)) adder_1 (.a(PROGRAM_COUNTER), .b(32'h4), .out(pc4_t));  // open: cin, cout
  Register #(.width(32)) PC (.D(multiplexer_1_out), .clk(clk), .Q(PROGRAM_COUNTER));  // open: en, clr
  Multiplexer #(.enable("false"), .width(32)) multiplexer_1 (
    .in0(pc4_t), .in1(ALUResult), .out(multiplexer_1_out), .sel(PCSel));
  control_logic control_logic_1 (
    .CSRWen(CSRWen), .PCSel(PCSel), .RegWEn(RegWEn), .ImmSel(control_logic_1_immsel), .BrUn(BrUn),
    .ASel(ASel), .BSel(BSel), .ALUSel(ALUSel), .MemRW(MemRW), .WBSel(WBSel), .CSRSel(CSRSel),
    .inst(INSTRUCTION), .BrEq(BrEq), .BrLt(BrLt));
  imm_gen imm_gen_1 (.inst(INSTRUCTION), .ImmSel(control_logic_1_immsel), .imm(imm));
  regfile regfile_1 (
    .rs1(INSTRUCTION[19:15]), .rs2(INSTRUCTION[24:20]), .rd(INSTRUCTION[11:7]), .Write_Data(WBSelOutput),
    .RegWEn(RegWEn), .clk(clk), .ra(ra), .sp(sp), .t0(t0), .t1(t1), .t2(t2), .s0(s0), .s1(s1), .a0(a0),
    .Read_Data_1(Read_Data_1), .Read_Data_2(Read_Data_2));
  branch_comp branch_comp_1 (.rs1(Read_Data_1), .rs2(Read_Data_2), .BrUn(BrUn), .BrEq(BrEq), .BrLt(BrLt));
  Multiplexer #(.enable("false"), .width(32)) multiplexer_2 (
    .in0(Read_Data_1), .in1(PROGRAM_COUNTER), .out(multiplexer_2_out), .sel(ASel));
  Multiplexer #(.enable("false"), .width(32)) multiplexer_3 (
    .in0(Read_Data_2), .in1(imm), .out(multiplexer_3_out), .sel(BSel));
  alu alu_1 (.Result(MEM_WRITE_ADDRESS), .A(multiplexer_2_out), .B(multiplexer_3_out), .ALUSel(ALUSel));
  // csr csr_1: pin names not known; wires that end beside it: CSR_address, CSR_din, CSRWen, clk, tohost
  Multiplexer #(.enable("false"), .width(32)) multiplexer_4 (
    .in0(Read_Data_1), .out(CSR_din), .sel(CSRSel));  // open: in1
  Multiplexer #(.enable("false"), .select(2), .width(8)) multiplexer_5 (
    .in0(MEM_READ_DATA[7:0]), .in1(MEM_READ_DATA[15:8]), .in2(MEM_READ_DATA[23:16]),
    .in3(MEM_READ_DATA[31:24]), .out(load_lb), .sel(MEM_WRITE_ADDRESS[1:0]));
  Multiplexer #(.enable("false"), .select(2), .width(16)) multiplexer_6 (
    .in0(MEM_READ_DATA[15:0]), .in2(MEM_READ_DATA[31:16]), .out(load_lh), .sel(MEM_WRITE_ADDRESS[1:0]));  // open: in1, in3
  Multiplexer #(.enable("false"), .select(2), .width(32)) multiplexer_7 (
    .in0(MEM_READ_DATA), .out(load_lw), .sel(MEM_WRITE_ADDRESS[1:0]));  // open: in1, in2, in3
  assign load_lb_ext = {{24{load_lb[7]}}, load_lb};  // Bit_Extender bit_extender_1
  assign load_lh_ext = {{16{load_lh[15]}}, load_lh};  // Bit_Extender bit_extender_2
  Multiplexer #(.enable("false"), .select(3), .width(32)) multiplexer_8 (
    .in0(load_lb_ext), .in1(load_lh_ext), .in2(load_lw), .out(rd_output_load), .sel(INSTRUCTION[14:12]));  // open: in3, in4, in5, in6, in7
  Shifter #(.width(32)) shifter_1 (.in(Read_Data_2), .\dist (5'b11000), .out(shifter_1_out));
  assign bit_extender_3_out = {{3{MEM_WRITE_ADDRESS[1]}}, MEM_WRITE_ADDRESS[1:0]};  // Bit_Extender bit_extender_3
  Shifter #(.width(32)) shifter_2 (.in(Read_Data_2), .\dist (5'b10000), .out(shifter_2_out));
  assign bit_extender_4_out = {{3{MEM_WRITE_ADDRESS[1]}}, MEM_WRITE_ADDRESS[1:0]};  // Bit_Extender bit_extender_4
  Shifter #(.shift("lr"), .width(32)) shifter_3 (.in(shifter_1_out), .\dist (5'b11000), .out(shifter_3_out));
  Shifter #(.width(5)) shifter_4 (.in(bit_extender_3_out), .\dist (3'b011), .out(shifter_4_out));
  Shifter #(.shift("lr"), .width(32)) shifter_5 (.in(shifter_2_out), .\dist (5'b10000), .out(shifter_5_out));
  Shifter #(.width(5)) shifter_6 (.in(bit_extender_4_out), .\dist (3'b011), .out(shifter_6_out));
  Shifter #(.width(32)) shifter_7 (.in(shifter_3_out), .\dist (shifter_4_out), .out(sb_store));
  Shifter #(.width(32)) shifter_8 (.in(shifter_5_out), .\dist (shifter_6_out), .out(sh_store));
  Multiplexer #(.enable("false"), .select(2), .width(32)) multiplexer_9 (
    .in0(rd_output_load), .in1(MEM_WRITE_ADDRESS), .in2(PC4), .out(WBSelOutput), .sel(WBSel));  // open: in3
  Multiplexer #(.enable("false"), .select(3), .width(32)) multiplexer_10 (
    .in0(sb_store), .in1(sh_store), .in2(Read_Data_2), .out(WriteData), .sel(INSTRUCTION[14:12]));  // open: in3, in4, in5, in6, in7

  // Other names for the same wires on the sheet: alu_result[31:0] = MEM_WRITE_ADDRESS; opcode[6:0] = INSTRUCTION[6:0];
  //   rd[4:0] = INSTRUCTION[11:7]; func3[2:0] = INSTRUCTION[14:12]; rs1[4:0] = INSTRUCTION[19:15];
  //   rs2[4:0] = INSTRUCTION[24:20]; sw_store[31:0] = Read_Data_2

  // Notes on the sheet:
  //   Output to IMEM
  //   IMEM (do **NOT** move this)
  //   Inputs from IMEM
  //   It is OK to move the PC, RegFile, ALU, MEM, Branch Comp, Imm Gen, and Control Logic to wherever is most convenient for you when constructing your CPU, and to delete this text
  //   Inputs/Outputs for testing. Do **NOT** move these.
  //   CSR INSTRUCTIONS
  //   LOAD INSTRUCTIONS
  //   Outputs To DMEM
  //   DMEM (do **NOT** move this)
  //   Inputs From DMEM
  //   STORE INSTRUCTIONS
endmodule
